// Logisim project ALU_GroupXX.circ as structural Verilog: 6 circuits, main circuit main
module main (
  output halt,
  output [8:0] counter,
  output [3:0] op,
  output [11:0] a,
  output [11:0] b,
  output [11:0] oracle,
  output [11:0] result,
  output err_oracle,
  output error,
  output ok,
  output start_delimiter
);

  wire and_1_out, and_2_out, clock_1_out, comparator_1_eq, comparator_2_eq;

  Clock clock_1 (.out(clock_1_out));
  Counter #(.width(9), .max('h1ff), .trigger("falling")) counter_1 (
    .Q(counter), .carry(halt), .clk(clock_1_out));  // open: load, D, count, clr
  RAM #(.addrWidth(12), .dataWidth(4), .bus("separate")) ram_1 (
    .addr({counter, 3'b000}), .data(op), .ld(1'b1));  // open: din, str, sel, clk, clr
  RAM #(.addrWidth(12), .dataWidth(12), .bus("separate")) ram_2 (
    .addr({counter, 3'b001}), .data(a), .ld(1'b1));  // open: din, str, sel, clk, clr
  RAM #(.addrWidth(12), .dataWidth(12), .bus("separate")) ram_3 (
    .addr({counter, 3'b010}), .data(b), .ld(1'b1));  // open: din, str, sel, clk, clr
  RAM #(.addrWidth(12), .dataWidth(12), .bus("separate")) ram_4 (
    .addr({counter, 3'b011}), .data(oracle), .ld(1'b1));  // open: din, str, sel, clk, clr
  RAM #(.addrWidth(12), .dataWidth(1), .bus("separate")) ram_5 (
    .addr({counter, 3'b100}), .data(err_oracle), .ld(1'b1));  // open: din, str, sel, clk, clr
  RAM #(.addrWidth(12), .dataWidth(1), .bus("separate")) ram_6 (
    .addr({counter, 3'b101}), .data(start_delimiter), .ld(1'b1));  // open: din, str, sel, clk, clr
  _12_bit_ALU u_12_bit_alu_1 (.ALU_code(op), .a(a), .b(b), .overflow(error), .result(result));
  Comparator #(.width(1), .mode("unsigned")) comparator_1 (
    .a(error), .b(err_oracle), .eq(comparator_1_eq));  // open: gt, lt
  Comparator #(.width(12)) comparator_2 (.a(result), .b(oracle), .eq(comparator_2_eq));  // open: gt, lt
  and and_1 (and_1_out, comparator_1_eq, error);
  and and_2 (and_2_out, comparator_2_eq, comparator_1_eq, ~error);  // AND_Gate
  or or_1 (ok, and_1_out, and_2_out);

  // Notes on the sheet:
  //   You must complete the circuit '12-bit ALU' instead.
  //   DO NOT EDIT THIS CIRCUIT!
endmodule

module _12_bit_ALU (
  input  [3:0] ALU_code,
  input  [11:0] a,
  input  [11:0] b,
  output [11:0] result,
  output overflow
);

  wire n12_bit_adder_1_overflow, subtraction_1_overflow;
  wire [11:0] and_1_out, equals_1_equals, greater_than_1_greater_than, less_than_1_lesser_than,
       n12_bit_adder_1_sum, or_1_out, subtraction_1_out_4;

  Greater_than greater_than_1 (.a(a), .b(b), .Greater_than(greater_than_1_greater_than));
  Equals equals_1 (.a(a), .b(b), .Equals(equals_1_equals));
  assign or_1_out = a | b;  // OR_Gate or_1, 12 bits wide
  assign and_1_out = b & a;  // AND_Gate and_1, 12 bits wide
  _12_Bit_Adder u_12_bit_adder_1 (.a(b), .b(a), .Sum(n12_bit_adder_1_sum), .Overflow(n12_bit_adder_1_overflow));
  Subtraction subtraction_1 (.a(a), .b(b), .Overflow(subtraction_1_overflow), .out_4(subtraction_1_out_4));
  Less_than less_than_1 (.a(a), .b(b), .Lesser_than(less_than_1_lesser_than));
  Multiplexer #(.select(4), .width(12), .enable("false")) multiplexer_1 (
    .in0({12{1'b0}}), .in1(or_1_out), .in2(and_1_out), .in3(n12_bit_adder_1_sum), .in4(subtraction_1_out_4),
    .in5(less_than_1_lesser_than), .in6(greater_than_1_greater_than), .in7(equals_1_equals), .out(result),
    .sel(ALU_code));  // open: in8, in9, in10, in11, in12, in13, in14, in15
  or or_2 (overflow, n12_bit_adder_1_overflow, subtraction_1_overflow);

  // Notes on the sheet:
  //   This circuit is used as a block in the main circuit, and its layout must remain unchanged. The circuit called "main" should be the main circuit of this file.
  //   Do not change the circuit appearance.
  //   DO NOT CHANGE THE INPUTS AND OUTPUTS OF THIS CIRCUIT!
  //   Do not add/remove inputs or outputs. Do not even change their location or orientation.
endmodule

// sub
module Subtraction (
  input  [11:0] a,
  input  [11:0] b,
  output Overflow,
  output [11:0] out_4
);

  wire [11:0] n12_bit_adder_1_sum, not_1_out;

  assign not_1_out = ~b;  // NOT_Gate not_1, 12 bits wide
  _12_Bit_Adder u_12_bit_adder_1 (.a(not_1_out), .b(12'h1), .Sum(n12_bit_adder_1_sum));  // open: Overflow
  _12_Bit_Adder u_12_bit_adder_2 (.a(a), .b(n12_bit_adder_1_sum), .Sum(out_4), .Overflow(Overflow));
endmodule

// lt
module Less_than (
  input  [11:0] a,
  input  [11:0] b,
  output [11:0] Lesser_than
);

  wire and_1_out, nand_1_out, nand_2_out, not_1_out;
  wire [11:0] equals_1_equals, multiplexer_1_out, multiplexer_2_out, multiplexer_3_out, multiplexer_4_out,
       multiplexer_5_out, subtraction_1_out_4, subtraction_2_out_4;

  Equals equals_1 (.a(b), .b(a), .Equals(equals_1_equals));
  not not_1 (not_1_out, equals_1_equals[0]);
  Subtraction subtraction_1 (.a(a), .b(b), .out_4(subtraction_1_out_4));  // open: Overflow
  Subtraction subtraction_2 (.a(a), .b(b), .out_4(subtraction_2_out_4));  // open: Overflow
  Multiplexer #(.width(12), .enable("false")) multiplexer_1 (
    .in0({12{1'b0}}), .in1(12'h1), .out(multiplexer_1_out), .sel(subtraction_1_out_4[11]));
  Multiplexer #(.width(12), .enable("false")) multiplexer_2 (
    .in0({12{1'b0}}), .in1(12'h1), .out(multiplexer_2_out), .sel(subtraction_2_out_4[11]));
  nand nand_1 (nand_1_out, a[11], ~b[11]);  // NAND_Gate
  nand nand_2 (nand_2_out, ~a[11], b[11]);  // NAND_Gate
  and and_1 (and_1_out, a[11], b[11]);
  Multiplexer #(.width(12), .enable("false")) multiplexer_3 (
    .in0(multiplexer_1_out), .in1(multiplexer_2_out), .out(multiplexer_3_out), .sel(and_1_out));
  Multiplexer #(.width(12), .enable("false")) multiplexer_4 (
    .in0({12{1'b0}}), .in1(multiplexer_5_out), .out(multiplexer_4_out), .sel(nand_2_out));
  Multiplexer #(.width(12), .enable("false")) multiplexer_5 (
    .in0({12{1'b0}}), .in1(multiplexer_3_out), .out(multiplexer_5_out), .sel(not_1_out));
  Multiplexer #(.width(12), .enable("false")) multiplexer_6 (
    .in0(12'h1), .in1(multiplexer_4_out), .out(Lesser_than), .sel(nand_1_out));
  // Pins of 1 and 12 bits meet at equals_1_equals
endmodule

// gt
module Greater_than (
  input  [11:0] a,
  input  [11:0] b,
  output [11:0] Greater_than
);

  wire and_1_out, nand_1_out, nand_2_out, not_1_out;
  wire [11:0] equals_1_equals, multiplexer_1_out, multiplexer_2_out, multiplexer_3_out, multiplexer_4_out,
       multiplexer_5_out, subtraction_1_out_4, subtraction_2_out_4;

  Equals equals_1 (.a(b), .b(a), .Equals(equals_1_equals));
  not not_1 (not_1_out, equals_1_equals[0]);
  Subtraction subtraction_1 (.a(a), .b(b), .out_4(subtraction_1_out_4));  // open: Overflow
  Subtraction subtraction_2 (.a(a), .b(b), .out_4(subtraction_2_out_4));  // open: Overflow
  Multiplexer #(.width(12), .enable("false")) multiplexer_1 (
    .in0(12'h1), .in1({12{1'b0}}), .out(multiplexer_1_out), .sel(subtraction_1_out_4[11]));
  Multiplexer #(.width(12), .enable("false")) multiplexer_2 (
    .in0(12'h1), .in1({12{1'b0}}), .out(multiplexer_2_out), .sel(subtraction_2_out_4[11]));
  nand nand_1 (nand_1_out, a[11], ~b[11]);  // NAND_Gate
  nand nand_2 (nand_2_out, ~a[11], b[11]);  // NAND_Gate
  and and_1 (and_1_out, a[11], b[11]);
  Multiplexer #(.width(12), .enable("false")) multiplexer_3 (
    .in0(multiplexer_1_out), .in1(multiplexer_2_out), .out(multiplexer_3_out), .sel(and_1_out));
  Multiplexer #(.width(12), .enable("false")) multiplexer_4 (
    .in0(12'h1), .in1(multiplexer_5_out), .out(multiplexer_4_out), .sel(nand_2_out));
  Multiplexer #(.width(12), .enable("false")) multiplexer_5 (
    .in0({12{1'b0}}), .in1(multiplexer_3_out), .out(multiplexer_5_out), .sel(not_1_out));
  Multiplexer #(.width(12), .enable("false")) multiplexer_6 (
    .in0({12{1'b0}}), .in1(multiplexer_4_out), .out(Greater_than), .sel(nand_1_out));
  // Pins of 1 and 12 bits meet at equals_1_equals
endmodule

// eq
module Equals (
  input  [11:0] a,
  input  [11:0] b,
  output [11:0] Equals
);

  wire nor_1_out;
  wire [11:0] subtraction_1_out_4;

  Subtraction subtraction_1 (.a(a), .b(b), .out_4(subtraction_1_out_4));  // open: Overflow
  nor nor_1 (nor_1_out, subtraction_1_out_4[0], subtraction_1_out_4[1], subtraction_1_out_4[2], subtraction_1_out_4[3], subtraction_1_out_4[4], subtraction_1_out_4[5], subtraction_1_out_4[6], subtraction_1_out_4[7], subtraction_1_out_4[8], subtraction_1_out_4[9], subtraction_1_out_4[10], subtraction_1_out_4[11]);
  Multiplexer #(.width(12), .enable("false")) multiplexer_1 (
    .in0({12{1'b0}}), .in1(12'h1), .out(Equals), .sel(nor_1_out));
endmodule
